# Fritzing sketch air polution checker (saved by Fritzing 0.9.10b)
circuit board: 6.39161cm x 5.65702cm

parts:
  Mod1 = Raspberry Pi Pico W
  OLED_I2C1 = OLED 128x64 I2C Monochrome Display
  U1 = WS2812 RGB LED matrix 2x2
  S1 = Round Pushbutton

nets:
  N1: Mod1.pin_21, OLED_I2C1.SDA
  N2: Mod1.pin_22, OLED_I2C1.SCK
  GND: Mod1.pin_23, Mod1.pin_28, Mod1.pin_33, Mod1.pin_38, OLED_I2C1.GND, U1.GND, S1.leg0
  N3: Mod1.pin_27, S1.leg1
  N4: Mod1.pin_29, U1.DIN
  VDD: Mod1.pin_36, OLED_I2C1.VDD, U1.VCC

custom parts:
  Raspberry Pi Pico W: Raspberry Pi Pico W. Based around the RP2040 microcontroller the Pico W is a low cost microcontroller device bringing Raspberry Pi quality, cost, and easy of use to the microcontroller space. The areas marked KEEPOUT in pcb silkscreen should not have traces running through them to avoid shorts on a soldered in module!
  WS2812 RGB LED matrix 2x2: WS2812 matrix 2x2
